# Fritzing sketch contra-tesla (saved by Fritzing 0.9.3b)

parts:
  M1 = DC Motor
  M2 = DC Motor
  M3 = DC Motor
  M4 = DC Motor
  Componente1 = Arduino Uno (Rev3)
  hc-sr1 = hc-sr04
  S1 = H-Bridge with L298N
  RHT1 = Humidity and Temperature Sensor RHT03
  GY1 = MPU-6050 Board GY-521 [form="♀ (female)" package=THT]
  TCRT2 = TCRT5000 digital module [part_number=151608]
  VCC1 = Battery block 9V
  TCRT3 = TCRT5000 digital module [part_number=151608]
  TCRT4 = TCRT5000 digital module [part_number=151608]
  J1 = Basic Servo
  J2 = Basic Servo

nets:
  N1: M1.pin_1, M2.pin_1, S1.M1-02
  N2: M1.pin_2, M2.pin_2, S1.M1-01
  N3: M3.pin_1, M4.pin_1, S1.M2-02
  N4: M3.pin_2, M4.pin_2, S1.M2-01
  N5: Componente1.A0, J1.pulse
  N6: Componente1.A1, J2.pulse
  N7: Componente1.A4/SDA, GY1.pin4
  N8: Componente1.A5/SCL, GY1.pin3
  N9: Componente1.D8, S1.IN4
  N10: Componente1.D9_PWM, TCRT3.DO2
  N11: Componente1.D10_PWM/SS, TCRT4.DO2
  N12: Componente1.D11_PWM/MOSI, hc-sr1.Echo
  N13: Componente1.D12/MISO, TCRT2.DO2
  N14: Componente1.D13/SCK, hc-sr1.Trig
  GND: Componente1.GND, hc-sr1.GND, S1.GND, RHT1.GND_1, GY1.pin2, VCC1.-
  N15: Componente1.D2, S1.IN1
  N16: Componente1.D3_PWM, S1.ENA
  N17: Componente1.D4, S1.IN2
  N18: Componente1.D5_PWM, S1.ENB
  N19: Componente1.D6_PWM, RHT1.Data-signal
  N20: Componente1.D7, S1.IN3
  VCC: Componente1.5V, hc-sr1.VCC, RHT1.Vcc, GY1.pin1
  VIN: Componente1.VIN, S1.12V, VCC1.+

notes:
  Motores ESQ
  Motores DIR

custom parts:
  H-Bridge with L298N: h-bridge
  MPU-6050 Board GY-521: Acelerometro y Giroscopio MPU-6050 Board GY-521
  TCRT5000 digital module: breakout board for TCRT5000 module, convert analog to digital - Uses TCRT5000 infrared reflectance sensor - Detection distance: 1mm~8mm - Focus distance: 2.5mm - Working voltage: 3.3V~12V - Uses wide voltage LM393 comparator - With multi-turn precision potentiometer to adjust the sensitivity - Current: > 15mA - Output type: Digital switch output (0, 1) - Suitable for watt-hour meter pulse data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
